# Fritzing sketch Clock (saved by Fritzing 0.9.2b)

parts:
  Teensy1 = Teensy 2.0
  IC1 = DS3231MZ Real Time Clock
  C1 = Capacitor [package=1210]
  U1 = HV5522PG [part_number=HV5522PG package=tqfp44]
  U2 = HV5522PG [part_number=HV5522PG package=tqfp44]
  R1 = Resistor [tolerance=±5% resistance=1k package="1206 [SMD]"]
  R2 = Resistor [tolerance=±5% resistance=10k package="1206 [SMD]"]
  Q1 = NPN-Transistor [package="SOT-23 [SMD]"]
  Q2 = NPN-Transistor [package="SOT-23 [SMD]"]
  R3 = Resistor [tolerance=±5% resistance=1k package="1206 [SMD]"]
  R4 = Resistor [tolerance=±5% resistance=10k package="1206 [SMD]"]
  Q3 = NPN-Transistor [package="SOT-23 [SMD]"]
  R5 = Resistor [tolerance=±5% resistance=1k package="1206 [SMD]"]
  R6 = Resistor [tolerance=±5% resistance=10k package="1206 [SMD]"]

nets:
  CLK5: Teensy1.B2, R5.Pin_0
  LE5: Teensy1.B3, R3.Pin_0
  DATA5: Teensy1.B7, R1.Pin_0
  SCL: Teensy1.D0, IC1.Pin_8
  SDA: Teensy1.D1, IC1.Pin_7
  5V: Teensy1.VCC, IC1.Pin_2, C1.1
  GND: Teensy1.GND, IC1.Pin_5, C1.2, U1.VSS, U2.VSS, Q1.2, Q2.2, Q3.2
  N1: U1.DATA_OUT, U2.DATA_IN
  CLK12: U1.CLK, U2.CLK, Q3.1, R6.Pin_0
  12V: U1.VDD, U2.VDD, R2.Pin_1, R4.Pin_1, R6.Pin_1
  LE12: U1.LE, U2.LE, Q2.1, R4.Pin_0
  DATA12: U1.DATA_IN, R2.Pin_0, Q1.1
  N2: R1.Pin_1, Q1.0
  N3: Q2.0, R3.Pin_1
  N4: Q3.0, R5.Pin_1

custom parts:
  DS3231MZ Real Time Clock: DS3231MZ Real Time Clock. SO-8 surface mount version.
  HV5522PG: High-Voltage Driver Chip (Open-Drain)
